# Fritzing sketch test (saved by Fritzing 0.9.2b)
breadboards: 1

parts:
  Raspberry_Pi1 = Raspberry Pi 2
  LED1 = LED - 5mm [color="Red (633nm)" package="5 mm [THT]"]
  R1 = Resistor [tolerance=±5% resistance=330 package=THT]

nets (from the schematic view):
  N1: Raspberry_Pi1.GPIO13, R1.Pin_1
  N2: Raspberry_Pi1.GND, LED1.anode
  N3: LED1.cathode, R1.Pin_0
